# Fritzing sketch final (saved by Fritzing 0.9.10b)
circuit board: 10cm x 7cm
breadboards: 1

parts:
  SW1 = Pushbutton [package="[THT]"]
  R3 = Resistor [tolerance=±5% resistance=1k power=0.25 package="1206 [SMD]"]
  R2 = Resistor [tolerance=±5% resistance=5.1k power=0.25 package="1206 [SMD]"]
  Arduino = Arduino Pro Micro (Clone)
  enc = ALPS-EC25-SRGP200200 [package=THT]
  R4 = Resistor [tolerance=±5% resistance=10k package="1206 [SMD]"]
  R5 = Resistor [tolerance=±5% resistance=10k package="1206 [SMD]"]
  OLED = OLED 128x64 I2C Monochrome Display
  R1 = Resistor [tolerance=±5% resistance=5.1k power=0.25 package="1206 [SMD]"]
  C3 = Ceramic Capacitor [capacitance=22pF voltage=10V package="100 mil [THT, multilayer]"]
  R6 = Resistor [tolerance=±5% resistance=10k power=0.25 package=THT]
  R7 = Resistor [tolerance=±5% resistance=10k power=0.25 package=THT]
  J2 = female pin header, 2 pins [form="♀ (female)"]
  C5 = Ceramic Capacitor [capacitance=100nF voltage=35V package="100 mil [THT, multilayer]"]
  C4 = Ceramic Capacitor [capacitance=100nF voltage=35V package="100 mil [THT, multilayer]"]

nets:
  GND: SW1.Pin_1, SW1.Pin_2, Arduino.GND, enc.pin2, OLED.GND, C3.0, J2.pin2, C5.0, C4.0
  N1: SW1.Pin_3, SW1.Pin_4, R3.Pin_0, Arduino.D8
  VCC: R3.Pin_1, R2.Pin_1, Arduino.VCC, R4.Pin_1, R5.Pin_1, OLED.VDD, R1.Pin_1, C3.1
  N2: R2.Pin_0, Arduino.D2, OLED.SDA
  N3: Arduino.TXO, R7.Pin_1, C5.1
  N4: Arduino.RXI, R6.Pin_1, C4.1
  N5: Arduino.D3, OLED.SCK, R1.Pin_0
  N6: Arduino.RST, J2.pin1
  N7: enc.pin1, R4.Pin_0, R6.Pin_0
  N8: enc.pin3, R5.Pin_0, R7.Pin_0

notes:
  BreakfastBerry
  v0.15

custom parts:
  ALPS-EC25-SRGP200200: Hollow-center shaft encoder enabling various combinations.
